# Fritzing sketch Real-PKE-Meter (saved by Fritzing 0.8.7b)
breadboards: 1

parts:
  Part1 = PowerBoost 500 Charger
  Part2 = Arduino Nano (Rev3.0)
  LED27 = LED - 5mm [color="Yellow (595nm)" package="5 mm [THT]"]
  LED32 = LED - 5mm [color="Yellow (595nm)" package="5 mm [THT]"]
  LED35 = LED - 5mm [color="Yellow (595nm)" package="5 mm [THT]"]
  LED36 = LED - 5mm [color="Yellow (595nm)" package="5 mm [THT]"]
  R8 = Resistor [tolerance=±5% resistance=330 package=THT]
  R9 = Resistor [tolerance=±5% resistance=330 package=THT]
  R10 = Resistor [tolerance=±5% resistance=330 package=THT]
  R11 = Resistor [tolerance=±5% resistance=330 package=THT]
  R12 = Resistor [tolerance=±5% resistance=330 package=THT]
  R13 = Resistor [tolerance=±5% resistance=330 package=THT]
  R14 = Resistor [tolerance=±5% resistance=330 package=THT]
  OLED_I2C1 = OLED 128x64 I2C Monochrome Display
  J1 = Piezo Speaker
  R15 = Resistor [tolerance=±5% resistance=330 package=THT]
  DHT1 = DHT22 Humidity and Temperature Sensor
  U3 = LIPO-1000mAh [package=lipo-1000]
  J2 = Basic Servo
  ANT1 = Antenna
  S1 = Toggle Switch [package=THT]
  S2 = Toggle Switch [package=THT]
  LED37 = LED - 5mm [color="Yellow (595nm)" package="5 mm [THT]"]
  LED38 = LED - 5mm [color="Yellow (595nm)" package="5 mm [THT]"]
  LED39 = LED - 5mm [color="Yellow (595nm)" package="5 mm [THT]"]
  LED40 = LED - 5mm [color="Yellow (595nm)" package="5 mm [THT]"]
  LED41 = LED - 5mm [color="Yellow (595nm)" package="5 mm [THT]"]
  LED42 = LED - 5mm [color="Yellow (595nm)" package="5 mm [THT]"]
  LED43 = LED - 5mm [color="Yellow (595nm)" package="5 mm [THT]"]
  LED44 = LED - 5mm [color="Yellow (595nm)" package="5 mm [THT]"]
  LED45 = LED - 5mm [color="Yellow (595nm)" package="5 mm [THT]"]
  LED46 = LED - 5mm [color="Yellow (595nm)" package="5 mm [THT]"]
  S3 = Pushbutton [package="[THT]"]
  S4 = Pushbutton [package="[THT]"]

nets:
  GND: Part1.GND, Part2.GND, LED27.cathode, LED32.cathode, LED35.cathode, LED36.cathode, OLED_I2C1.GND, J1.pin1, DHT1.GND, U3.-, J2.gnd, LED37.cathode, LED38.cathode, LED39.cathode, LED40.cathode, LED41.cathode, LED42.cathode, LED43.cathode, LED44.cathode, LED45.cathode, LED46.cathode, S3.Pin_1, S3.Pin_2, S4.Pin_3, S4.Pin_4
  N1: Part1.VBAT, U3.+
  N2: Part1.5.0V, S2.L1
  N3: Part2.D2, R8.Pin_1
  N4: Part2.D3, R9.Pin_1
  N5: Part2.D4, R14.Pin_1
  N6: Part2.D5, R13.Pin_1
  N7: Part2.D6, R12.Pin_1
  N8: Part2.D7, R11.Pin_1
  N9: Part2.D8, R10.Pin_1
  N10: Part2.D9, S3.Pin_3, S3.Pin_4
  N11: Part2.D10, J2.pulse
  N12: Part2.D11/MOSI, DHT1.NULL
  N13: Part2.D12/MISO, R15.Pin_1
  VDD: Part2.VIN, OLED_I2C1.VDD, DHT1.VDD, J2.vcc, S2.L2
  N14: Part2.A5, OLED_I2C1.SCK
  N15: Part2.A4, OLED_I2C1.SDA
  N16: Part2.A0, ANT1.antenna_lead
  N17: Part2.D13/SCK, S4.Pin_1, S4.Pin_2
  N18: LED27.anode, LED35.anode, R13.Pin_0
  N19: LED32.anode, LED36.anode, R12.Pin_0
  N20: R8.Pin_0, LED41.anode, LED44.anode
  N21: R9.Pin_0, LED43.anode, LED46.anode
  N22: R10.Pin_0, LED38.anode, LED40.anode
  N23: R11.Pin_0, LED37.anode, LED39.anode
  N24: R14.Pin_0, LED42.anode, LED45.anode
  N25: J1.pin2, S1.L2
  N26: R15.Pin_0, S1.L1

custom parts:
  PowerBoost 500 Charger: The PowerBoost 500C is a little DC/DC boost converter module that can be powered by any 3.7V LiIon/LiPoly battery, and convert the battery output to 5.2V DC for running your 5V projects. At its heart is a TPS61090 boost converter from TI. This boost converter chip has some really nice extras such as low battery detection, 2A internal switch, synchronous conversion, excellent efficiency, and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
